# Fritzing sketch Fritzing_Diagram (saved by Fritzing 0.9.6b)

parts:
  LCD_Keypad_Shield = LCD Keypad Shield
  Servo_SG90 = Basic Servo
  R2 = Resistor [tolerance=±5% resistance=10k package="0603 [SMD]"]
  TIL32_940nm_5mm = smd LED [color="Infrared (850nm)" current=0.030 package="1206 [SMD]"]
  TIL78_940nm_5mm = Photodiode 5mm Black [package="5 mm [THT]"]
  TIL78_940nm_5mm1 = Photodiode 5mm Black [package="5 mm [THT]"]
  TIL32_940nm_5mm1 = smd LED [color="Infrared (850nm)" current=0.030 package="1206 [SMD]"]
  TIL78_940nm_5mm5 = Photodiode 5mm Black [package="5 mm [THT]"]
  TIL32_940nm_5mm3 = smd LED [color="Infrared (850nm)" current=0.030 package="1206 [SMD]"]
  R3 = Resistor [tolerance=±5% resistance=330 package="0603 [SMD]"]
  R4 = Resistor [tolerance=±5% resistance=330 package="0603 [SMD]"]
  R5 = Resistor [tolerance=±5% resistance=330 package="0603 [SMD]"]
  R6 = Resistor [tolerance=±5% resistance=10k package="0603 [SMD]"]
  R7 = Resistor [tolerance=±5% resistance=10k package="0603 [SMD]"]

nets:
  N1: LCD_Keypad_Shield.A1, Servo_SG90.vcc, R2.Pin_0, TIL78_940nm_5mm.cathode
  N2: LCD_Keypad_Shield.A2, TIL78_940nm_5mm1.cathode
  N3: LCD_Keypad_Shield.A3, TIL78_940nm_5mm5.cathode, R3.Pin_0, R4.Pin_0, R5.Pin_0, R7.Pin_1
  N4: LCD_Keypad_Shield.A5(CLK), Servo_SG90.pulse
  GND: LCD_Keypad_Shield.GND, Servo_SG90.gnd, TIL32_940nm_5mm.cathode, TIL78_940nm_5mm.anode, TIL78_940nm_5mm1.anode, TIL32_940nm_5mm1.cathode, TIL78_940nm_5mm5.anode, TIL32_940nm_5mm3.cathode
  N5: R2.Pin_1, R6.Pin_1, R7.Pin_0

custom parts:
  LCD Keypad Shield: It consists of a 1602 white character blue backlight LCD. The keypad consists of 5 keys — select, up, right, down and left. To save the digital IO pins, the keypad interface uses only one ADC channel. The key value is read through a 5 stage voltage divider.
  Photodiode 5mm Black: Photodiode 5mm Black/ Transparent
